# Fritzing sketch ASKRmtCntrlDcdr (saved by Fritzing 0.9.3b)
breadboards: 1

parts:
  Power_plug1 = Power plug [part_number=5V]
  R1 = Resistor [tolerance=±5% resistance=1k package=THT]
  R2 = Resistor [tolerance=±5% resistance=1k package=THT]
  LED1 = LED - 5mm [color="Blue (505nm)" package="5 mm [THT]"]
  R3 = Resistor [tolerance=±5% resistance=1k package=THT]
  R4 = Resistor [tolerance=±5% resistance=1k package=THT]
  R5 = Resistor [tolerance=±5% resistance=1k package=THT]
  LED2 = LED - 5mm [color="Blue (505nm)" package="5 mm [THT]"]
  LED3 = LED - 5mm [color="Blue (505nm)" package="5 mm [THT]"]
  LED4 = LED - 5mm [color="Blue (505nm)" package="5 mm [THT]"]
  LED5 = LED - 5mm [color="Red (633nm)" package="5 mm [THT]"]
  R6 = Resistor [tolerance=±5% resistance=1k package=THT]
  S1 = Pushbutton [package="[THT]"]
  SW1 = DIP SWITCH [package=dipswitch-02]
  C1 = Ceramic Capacitor [capacitance=100nF package="100 mil [THT, multilayer]"]
  C2 = Ceramic Capacitor [capacitance=100nF package="100 mil [THT, multilayer]"]
  J1 = double row female pin header, 2 pins [form="♀ (female)" part_number="Serial Output"]
  C3 = Ceramic Capacitor [capacitance=100nF package="100 mil [THT, multilayer]"]
  U2 = XD-RF-5V [package=THT]
  U1 = ATmega8A [package=tqfp]
  ANT1 = Antenna

nets:
  GND: Power_plug1.GND, R2.Pin_1, R3.Pin_1, R4.Pin_1, R5.Pin_1, R6.Pin_1, S1.Pin_3, S1.Pin_4, SW1.1, SW1.2, J1.pin1, U2.GND, U1.GND, U1.AGND
  VCC: Power_plug1.VCC, C1.0, C2.1, C3.1, U2.VCC, U1.VCC, U1.AVCC, U1.AREF
  N1: R1.Pin_0, U1.PD2(INT0)
  N2: R1.Pin_1, U2.DATA
  N3: R2.Pin_0, LED1.cathode
  N4: LED1.anode, U1.PC3(ADC3)
  N5: R3.Pin_0, LED2.cathode
  N6: R4.Pin_0, LED3.cathode
  N7: R5.Pin_0, LED4.cathode
  N8: LED2.anode, U1.PC2(ADC2)
  N9: LED3.anode, U1.PC1(ADC1)
  N10: LED4.anode, U1.PC0(ADC0)
  N11: LED5.cathode, R6.Pin_0
  N12: LED5.anode, U1.PB3(MOSI_OC2)
  N13: S1.Pin_1, S1.Pin_2, C3.0, U1.PB2(SS_OC1B)
  N14: SW1.3, C2.0, U1.PB1(OC1A)
  N15: SW1.4, C1.1, U1.PB0(ICP)
  N16: J1.pin2, U1.PD1(TXD)
  N17: U2.Attenna, ANT1.antenna_lead

notes:
  By Mohammad Yousefi - vahidyou@gmail.com

custom parts:
  XD-RF-5V: This is 433Mhz RF transmitter with receiver kit for Arduino ARM MCU wireless Application environment: Remote control switch, receiver module, motorcycles, automobile anti-theft products, home security products, electric doors, shutter doors, windows, remote control socket, remote control LED, remote audio remote control electric doors, garage door remote control, remote control retractable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
